# Fritzing sketch diagram (saved by Fritzing 0.9.3b)
breadboards: 1

parts:
  R1 = Resistor [tolerance=±5% resistance=100 package=THT]
  R2 = Resistor [tolerance=±5% resistance=10k package=THT]
  R3 = Resistor [tolerance=±5% resistance=10k package=THT]
  U1 = attiny85 [package=dip]
  Emitter = LED - 5mm [color="Infrared (940nm)" package="5 mm [THT]"]
  Receiver_A = LED - 5mm [color="Infrared (940nm)" package="5 mm [THT]"]
  Receiver_B = LED - 5mm [color="Infrared (940nm)" package="5 mm [THT]"]
  RELAY = KY-019 5V Relay Module [package="Breakout board"]
  DEBUG_SIGNAL_A = LED - 5mm [color="Red (633nm)" package="5 mm [THT]"]
  DEBUG_SIGNAL_B = LED - 5mm [color="Red (633nm)" package="5 mm [THT]"]
  R4 = Resistor [tolerance=±5% resistance=330 package=THT]
  R5 = Resistor [tolerance=±5% resistance=330 package=THT]
  Lamp = Header 2 [package=screwterminal-3.5mm-2_lock]
  part = AC Power [voltage=220 frequency=60]

nets:
  GND: R1.Pin_0, R2.Pin_0, R3.Pin_0, U1.Pin_4, RELAY.-, R4.Pin_0, R5.Pin_0
  N1: R1.Pin_1, Emitter.cathode
  N2: R2.Pin_1, Receiver_A.cathode
  N3: R3.Pin_1, Receiver_B.cathode
  N4: U1.Pin_2, Receiver_A.anode
  N5: U1.Pin_3, Receiver_B.anode
  DEBUG pin: U1.Pin_5, U1.Pin_6, DEBUG_SIGNAL_A.anode, DEBUG_SIGNAL_B.anode
  N6: U1.Pin_7, RELAY.S
  5V: U1.Pin_8, Emitter.anode, RELAY.+
  N7: RELAY.Common, Lamp.1
  N8: RELAY.NO, part.V-
  N9: DEBUG_SIGNAL_A.cathode, R4.Pin_1
  N10: DEBUG_SIGNAL_B.cathode, R5.Pin_1
  N11: Lamp.2, part.V+

custom parts:
  KY-019 5V Relay Module: KY-019 5V Relay module, used to control AC circuits.
